// Logisim project CPU.circ as structural Verilog: 14 circuits, main circuit main
module main (
  output [7:0] out_1
);

  wire alu_2_zero, and_1_out, clock_1_out, clock_2_out, ReiniciarPC_out;
  wire [3:0] undriven;
  wire [7:0] A_q, alu_1_s0, alu_2_s0, B_q, multiplexer_1_out, ram_1_dout, sumador_1_s0, sumador_2_s0;

  Clock clock_1 (.out(clock_1_out));
  Register PC (.D(multiplexer_1_out), .en(clock_1_out), .clk(clock_1_out), .Q(out_1), .clr(ReiniciarPC_out));
  Button ReiniciarPC (.out(ReiniciarPC_out));
  Sumador sumador_1 (
    .B1(out_1[1]), .A0(1'b1), .B0(out_1[0]), .A7(1'b0), .B7(out_1[7]), .A6(1'b0), .B6(out_1[6]), .A5(1'b0),
    .B5(out_1[5]), .A4(1'b0), .B4(out_1[4]), .A3(1'b0), .B3(out_1[3]), .A2(1'b0), .B2(out_1[2]), .A1(1'b0),
    .S1(sumador_1_s0[1]), .S0(sumador_1_s0[0]), .S7(sumador_1_s0[7]), .S6(sumador_1_s0[6]),
    .S5(sumador_1_s0[5]), .S4(sumador_1_s0[4]), .S3(sumador_1_s0[3]), .S2(sumador_1_s0[2]));  // open: Cout
  _7_Segment_Display u_7_segment_display_1 ();  // open: g, f, a, b, e, d, c, dp
  // BCD_to_7_Segment_decoder bcd_to_7_segment_decoder_1: pin names not known
  ROM rom_1 (.addr(out_1));  // open: data
  _7_Segment_Display u_7_segment_display_2 ();  // open: g, f, a, b, e, d, c, dp
  // BCD_to_7_Segment_decoder bcd_to_7_segment_decoder_2: pin names not known
  // Binary_to_BCD_converter #(.binvalue(8)) binary_to_bcd_converter_1: pin names not known; wires that end beside it: out_1
  _7_Segment_Display u_7_segment_display_3 ();  // open: g, f, a, b, e, d, c, dp
  // BCD_to_7_Segment_decoder bcd_to_7_segment_decoder_3: pin names not known
  Clock clock_2 (.out(clock_2_out));
  Register A (.clk(clock_2_out), .Q(A_q));  // open: D, en, clr
  Register B (.clk(clock_2_out), .Q(B_q));  // open: D, en, clr
  ALU alu_1 (
    .A3(A_q[3]), .A2(A_q[2]), .A1(A_q[1]), .A0(A_q[0]), .B7(B_q[7]), .B6(B_q[6]), .B5(B_q[5]), .B4(B_q[4]),
    .B3(B_q[3]), .B2(B_q[2]), .B1(B_q[1]), .B0(B_q[0]), .A7(A_q[7]), .A6(A_q[6]), .A5(A_q[5]), .A4(A_q[4]),
    .S7(alu_1_s0[7]), .S6(alu_1_s0[6]), .S5(alu_1_s0[5]), .S4(alu_1_s0[4]), .S3(alu_1_s0[3]),
    .S2(alu_1_s0[2]), .S1(alu_1_s0[1]), .S0(alu_1_s0[0]));  // open: C3, C2, C1, C0, Zero, Cout
  ALU alu_2 (
    .C3(undriven[3]), .C2(undriven[2]), .C1(undriven[1]), .C0(undriven[0]), .Zero(alu_2_zero),
    .S7(alu_2_s0[7]), .S6(alu_2_s0[6]), .S5(alu_2_s0[5]), .S4(alu_2_s0[4]), .S3(alu_2_s0[3]),
    .S2(alu_2_s0[2]), .S1(alu_2_s0[1]), .S0(alu_2_s0[0]));  // open: A3, A2, A1, A0, B7, B6, B5, B4, B3, B2, B1, B0, A7, A6, A5, A4, Cout
  Sumador sumador_2 (
    .A0(sumador_1_s0[0]), .A7(sumador_1_s0[7]), .A6(sumador_1_s0[6]), .A5(sumador_1_s0[5]),
    .A4(sumador_1_s0[4]), .A3(sumador_1_s0[3]), .A2(sumador_1_s0[2]), .A1(sumador_1_s0[1]),
    .S1(sumador_2_s0[1]), .S0(sumador_2_s0[0]), .S7(sumador_2_s0[7]), .S6(sumador_2_s0[6]),
    .S5(sumador_2_s0[5]), .S4(sumador_2_s0[4]), .S3(sumador_2_s0[3]), .S2(sumador_2_s0[2]));  // open: B1, B0, B7, B6, B5, B4, B3, B2, Cout
  Multiplexer #(.width(8)) multiplexer_1 (
    .in0(sumador_1_s0), .in1(sumador_2_s0), .out(multiplexer_1_out), .sel(and_1_out));
  and and_1 (and_1_out, 1'b1, alu_2_zero);
  Register S (.D(alu_1_s0));  // open: en, clk, Q, clr
  RAM ram_1 (.addr(alu_2_s0), .dout(ram_1_dout));  // open: we, oe, clk, din
  ALU alu_3 ();  // open: A3, A2, A1, A0, B7, B6, B5, B4, B3, B2, B1, B0, C3, C2, C1, C0, A7, A6, A5, A4, Zero, Cout, S7, S6, S5, S4, S3, S2, S1, S0
  Multiplexer #(.width(8)) multiplexer_2 (.in0(ram_1_dout), .in1(alu_2_s0));  // open: out, sel

  // Notes on the sheet:
  //   1
  //   ADD-PC
endmodule

module ALU (
  input  C3,
  input  C2,
  input  C1,
  input  C0,
  input  A7,
  input  A6,
  input  A5,
  input  A4,
  input  A3,
  input  A2,
  input  A1,
  input  A0,
  input  B7,
  input  B6,
  input  B5,
  input  B4,
  input  B3,
  input  B2,
  input  B1,
  input  B0,
  output Cout,
  output S7,
  output S6,
  output S5,
  output S4,
  output S3,
  output S2,
  output Zero,
  output S1,
  output S0
);

  wire not_1_out;
  wire [1:0] sumador_1_cout;
  wire [6:0] sumador_1_s0, sumador_1_s1, sumador_1_s2, sumador_1_s3, sumador_1_s4, sumador_1_s5,
       sumador_1_s6, sumador_1_s7;

  ExactlyOne xor_1 (
    .out(Zero), .in0(A7), .in1(A6), .in2(A5), .in3(A4), .in4(A3), .in5(A2), .in6(A1), .in7(A0),
    .in8(not_1_out), .in9(B7), .in10(B6), .in11(B5), .in12(B4), .in13(B3), .in14(B2), .in15(B1), .in16(B0));
  not not_1 (not_1_out, 1'b0);
  Sumador sumador_1 (
    .B1(B1), .A0(A0), .B0(B0), .A7(A7), .B7(B7), .A6(A6), .B6(B6), .A5(A5), .B5(B5), .A4(A4), .B4(B4),
    .A3(A3), .B3(B3), .A2(A2), .B2(B2), .A1(A1), .S1(sumador_1_s1[0]), .S0(sumador_1_s0[0]),
    .Cout(sumador_1_cout[0]), .S7(sumador_1_s7[0]), .S6(sumador_1_s6[0]), .S5(sumador_1_s5[0]),
    .S4(sumador_1_s4[0]), .S3(sumador_1_s3[0]), .S2(sumador_1_s2[0]));
  Restador restador_1 (
    .B1(B1), .A0(A0), .B0(B0), .A7(A7), .B7(B7), .A6(A6), .B6(B6), .A5(A5), .B5(B5), .A4(A4), .B4(B4),
    .A3(A3), .B3(B3), .A2(A2), .B2(B2), .A1(A1), .S1(sumador_1_s1[1]), .S0(sumador_1_s0[1]),
    .Cout(sumador_1_cout[1]), .S7(sumador_1_s7[1]), .S6(sumador_1_s6[1]), .S5(sumador_1_s5[1]),
    .S4(sumador_1_s4[1]), .S3(sumador_1_s3[1]), .S2(sumador_1_s2[1]));
  CompOR compor_1 (
    .B1(B1), .A0(A0), .B0(B0), .A7(A7), .B7(B7), .A6(A6), .B6(B6), .A5(A5), .B5(B5), .A4(A4), .B4(B4),
    .A3(A3), .B3(B3), .A2(A2), .B2(B2), .A1(A1), .S1(sumador_1_s1[2]), .S0(sumador_1_s0[2]),
    .S7(sumador_1_s7[2]), .S6(sumador_1_s6[2]), .S5(sumador_1_s5[2]), .S4(sumador_1_s4[2]),
    .S3(sumador_1_s3[2]), .S2(sumador_1_s2[2]));
  CompAND compand_1 (
    .B1(B1), .A0(A0), .B0(B0), .A7(A7), .B7(B7), .A6(A6), .B6(B6), .A5(A5), .B5(B5), .A4(A4), .B4(B4),
    .A3(A3), .B3(B3), .A2(A2), .B2(B2), .A1(A1), .S1(sumador_1_s1[3]), .S0(sumador_1_s0[3]),
    .S7(sumador_1_s7[3]), .S6(sumador_1_s6[3]), .S5(sumador_1_s5[3]), .S4(sumador_1_s4[3]),
    .S3(sumador_1_s3[3]), .S2(sumador_1_s2[3]));
  CompXOR compxor_1 (
    .B1(B1), .A0(A0), .B0(B0), .A7(A7), .B7(B7), .A6(A6), .B6(B6), .A5(A5), .B5(B5), .A4(A4), .B4(B4),
    .A3(A3), .B3(B3), .A2(A2), .B2(B2), .A1(A1), .S1(sumador_1_s1[4]), .S0(sumador_1_s0[4]),
    .S7(sumador_1_s7[4]), .S6(sumador_1_s6[4]), .S5(sumador_1_s5[4]), .S4(sumador_1_s4[4]),
    .S3(sumador_1_s3[4]), .S2(sumador_1_s2[4]));
  CompNAND compnand_1 (
    .B1(B1), .A0(A0), .B0(B0), .A7(A7), .B7(B7), .A6(A6), .B6(B6), .A5(A5), .B5(B5), .A4(A4), .B4(B4),
    .A3(A3), .B3(B3), .A2(A2), .B2(B2), .A1(A1), .S1(sumador_1_s1[5]), .S0(sumador_1_s0[5]),
    .S7(sumador_1_s7[5]), .S6(sumador_1_s6[5]), .S5(sumador_1_s5[5]), .S4(sumador_1_s4[5]),
    .S3(sumador_1_s3[5]), .S2(sumador_1_s2[5]));
  CompNOR compnor_1 (
    .B1(B1), .A0(A0), .B0(B0), .A7(A7), .B7(B7), .A6(A6), .B6(B6), .A5(A5), .B5(B5), .A4(A4), .B4(B4),
    .A3(A3), .B3(B3), .A2(A2), .B2(B2), .A1(A1), .S1(sumador_1_s1[6]), .S0(sumador_1_s0[6]),
    .S7(sumador_1_s7[6]), .S6(sumador_1_s6[6]), .S5(sumador_1_s5[6]), .S4(sumador_1_s4[6]),
    .S3(sumador_1_s3[6]), .S2(sumador_1_s2[6]));
  SelectorMUX16 selectormux16_1 (.in_1({C3, C2, C1, C0}), .in_2({{14{1'b0}}, sumador_1_cout}), .S(Cout));
  SelectorMUX16 selectormux16_2 (.in_1({C3, C2, C1, C0}), .in_2({{9{1'b0}}, sumador_1_s7}), .S(S7));
  SelectorMUX16 selectormux16_3 (.in_1({C3, C2, C1, C0}), .in_2({{9{1'b0}}, sumador_1_s6}), .S(S6));
  SelectorMUX16 selectormux16_4 (.in_1({C3, C2, C1, C0}), .in_2({{9{1'b0}}, sumador_1_s5}), .S(S5));
  SelectorMUX16 selectormux16_5 (.in_1({C3, C2, C1, C0}), .in_2({{9{1'b0}}, sumador_1_s4}), .S(S4));
  SelectorMUX16 selectormux16_6 (.in_1({C3, C2, C1, C0}), .in_2({{9{1'b0}}, sumador_1_s3}), .S(S3));
  SelectorMUX16 selectormux16_7 (.in_1({C3, C2, C1, C0}), .in_2({{9{1'b0}}, sumador_1_s2}), .S(S2));
  SelectorMUX16 selectormux16_8 (.in_1({C3, C2, C1, C0}), .in_2({{9{1'b0}}, sumador_1_s1}), .S(S1));
  SelectorMUX16 selectormux16_9 (.in_1({C3, C2, C1, C0}), .in_2({{9{1'b0}}, sumador_1_s0}), .S(S0));
endmodule

module ALUTEST (
  input  in_1,
  input  in_2,
  input  in_3,
  input  in_4,
  input  in_5,
  input  in_6,
  input  in_7,
  input  in_8,
  input  in_9,
  input  in_10,
  input  in_11,
  input  in_12,
  input  in_13,
  input  in_14,
  input  in_15,
  input  in_16,
  input  in_17,
  input  in_18,
  input  in_19,
  input  in_20,
  output out_21,
  output out_22,
  output out_23,
  output out_24,
  output out_25,
  output out_26,
  output out_27,
  output out_28,
  output out_29
);

  wire alu_1_zero;

  ALU alu_1 (
    .A3(in_9), .A2(in_10), .A1(in_11), .A0(in_12), .B7(in_13), .B6(in_14), .B5(in_15), .B4(in_16),
    .B3(in_17), .B2(in_18), .B1(in_19), .B0(in_20), .C3(in_1), .C2(in_2), .C1(in_3), .C0(in_4), .A7(in_5),
    .A6(in_6), .A5(in_7), .A4(in_8), .Zero(alu_1_zero), .Cout(out_21), .S7(out_22), .S6(out_23), .S5(out_24),
    .S4(out_25), .S3(out_26), .S2(out_27), .S1(out_28), .S0(out_29));
  LED Zero (.in(alu_1_zero));

  // Notes on the sheet:
  //   0 - Sumar
  //   1 - Restar
  //   2 - OR
  //   3 - AND
  //   4 - XOR
  //   5 - NAND
endmodule

module FullAdderCasero (
  input  A,
  input  B,
  input  Cin,
  output S,
  output Cout
);

  wire and_1_out, and_2_out, xor_1_out;

  xor xor_1 (xor_1_out, A, B);
  Adder adder_1 ();  // open: a, b, out, cin, cout
  xor xor_2 (S, xor_1_out, Cin);
  and and_1 (and_1_out, Cin, xor_1_out);
  and and_2 (and_2_out, B, A);
  or or_1 (Cout, and_1_out, and_2_out);

  // Notes on the sheet:
  //   Full Adder Casero
endmodule

module Sumador (
  input  A7,
  input  A6,
  input  A5,
  input  A4,
  input  A3,
  input  A2,
  input  A1,
  input  A0,
  input  B7,
  input  B6,
  input  B5,
  input  B4,
  input  B3,
  input  B2,
  input  B1,
  input  B0,
  output Cout,
  output S7,
  output S6,
  output S5,
  output S4,
  output S3,
  output S2,
  output S1,
  output S0
);

  wire fulladdercasero_2_cout, fulladdercasero_3_cout, fulladdercasero_4_cout, fulladdercasero_5_cout,
       fulladdercasero_6_cout, fulladdercasero_7_cout, fulladdercasero_8_cout;

  FullAdderCasero fulladdercasero_1 (.A(A7), .B(B7), .Cin(fulladdercasero_2_cout), .S(S7), .Cout(Cout));
  FullAdderCasero fulladdercasero_2 (
    .A(A6), .B(B6), .Cin(fulladdercasero_3_cout), .S(S6), .Cout(fulladdercasero_2_cout));
  FullAdderCasero fulladdercasero_3 (
    .A(A5), .B(B5), .Cin(fulladdercasero_4_cout), .S(S5), .Cout(fulladdercasero_3_cout));
  Adder adder_1 ();  // open: a, b, out, cin, cout
  FullAdderCasero fulladdercasero_4 (
    .A(A4), .B(B4), .Cin(fulladdercasero_5_cout), .S(S4), .Cout(fulladdercasero_4_cout));
  FullAdderCasero fulladdercasero_5 (
    .A(A3), .B(B3), .Cin(fulladdercasero_6_cout), .S(S3), .Cout(fulladdercasero_5_cout));
  FullAdderCasero fulladdercasero_6 (
    .A(A2), .B(B2), .Cin(fulladdercasero_7_cout), .S(S2), .Cout(fulladdercasero_6_cout));
  FullAdderCasero fulladdercasero_7 (
    .A(A1), .B(B1), .Cin(fulladdercasero_8_cout), .S(S1), .Cout(fulladdercasero_7_cout));
  FullAdderCasero fulladdercasero_8 (.A(A0), .B(B0), .Cin(1'b0), .S(S0), .Cout(fulladdercasero_8_cout));

  // Notes on the sheet:
  //   Sumador Casero
endmodule

module Restador (
  input  A7,
  input  A6,
  input  A5,
  input  A4,
  input  A3,
  input  A2,
  input  A1,
  input  A0,
  input  B7,
  input  B6,
  input  B5,
  input  B4,
  input  B3,
  input  B2,
  input  B1,
  input  B0,
  output Cout,
  output S7,
  output S6,
  output S5,
  output S4,
  output S3,
  output S2,
  output S1,
  output S0
);

  wire fulladdercasero_1_cout, fulladdercasero_2_cout, fulladdercasero_3_cout, fulladdercasero_4_cout,
       fulladdercasero_5_cout, fulladdercasero_6_cout, fulladdercasero_7_cout, fulladdercasero_8_cout,
       not_2_out, not_3_out, not_4_out, not_5_out, not_6_out, not_7_out, not_8_out, not_9_out, not_10_out;

  not not_1 (Cout, fulladdercasero_1_cout);
  not not_2 (not_2_out, B7);
  FullAdderCasero fulladdercasero_1 (
    .A(A7), .B(not_2_out), .Cin(fulladdercasero_2_cout), .S(S7), .Cout(fulladdercasero_1_cout));
  not not_3 (not_3_out, B6);
  FullAdderCasero fulladdercasero_2 (
    .A(A6), .B(not_3_out), .Cin(fulladdercasero_3_cout), .S(S6), .Cout(fulladdercasero_2_cout));
  FullAdderCasero fulladdercasero_3 (
    .A(A5), .B(not_4_out), .Cin(fulladdercasero_4_cout), .S(S5), .Cout(fulladdercasero_3_cout));
  not not_4 (not_4_out, B5);
  Subtractor subtractor_1 ();  // open: a, b, out, bin, bout
  not not_5 (not_5_out, B4);
  FullAdderCasero fulladdercasero_4 (
    .A(A4), .B(not_5_out), .Cin(fulladdercasero_5_cout), .S(S4), .Cout(fulladdercasero_4_cout));
  not not_6 (not_6_out, B3);
  FullAdderCasero fulladdercasero_5 (
    .A(A3), .B(not_6_out), .Cin(fulladdercasero_6_cout), .S(S3), .Cout(fulladdercasero_5_cout));
  not not_7 (not_7_out, B2);
  FullAdderCasero fulladdercasero_6 (
    .A(A2), .B(not_7_out), .Cin(fulladdercasero_7_cout), .S(S2), .Cout(fulladdercasero_6_cout));
  FullAdderCasero fulladdercasero_7 (
    .A(A1), .B(not_8_out), .Cin(fulladdercasero_8_cout), .S(S1), .Cout(fulladdercasero_7_cout));
  not not_8 (not_8_out, B1);
  not not_9 (not_9_out, B0);
  not not_10 (not_10_out, 1'b0);
  FullAdderCasero fulladdercasero_8 (.A(A0), .B(not_9_out), .Cin(not_10_out), .S(S0), .Cout(fulladdercasero_8_cout));

  // Notes on the sheet:
  //   Restador Casero
endmodule

module CompOR (
  input  A7,
  input  B7,
  input  A6,
  input  B6,
  input  A5,
  input  B5,
  input  A4,
  input  B4,
  input  A3,
  input  B3,
  input  A2,
  input  B2,
  input  A1,
  input  B1,
  input  A0,
  input  B0,
  output S7,
  output S6,
  output S5,
  output S4,
  output S3,
  output S2,
  output S1,
  output S0
);

  or or_1 (S7, A7, B7);
  or or_2 (S6, A6, B6);
  or or_3 (S5, A5, B5);
  or or_4 (S4, A4, B4);
  or or_5 (S3, A3, B3);
  or or_6 (S2, A2, B2);
  or or_7 (S1, A1, B1);
  or or_8 (S0, A0, B0);
endmodule

module CompAND (
  input  A7,
  input  B7,
  input  A6,
  input  B6,
  input  A5,
  input  B5,
  input  A4,
  input  B4,
  input  A3,
  input  B3,
  input  A2,
  input  B2,
  input  A1,
  input  B1,
  input  A0,
  input  B0,
  output S7,
  output S6,
  output S5,
  output S4,
  output S3,
  output S2,
  output S1,
  output S0
);

  and and_1 (S7, A7, B7);
  and and_2 (S6, A6, B6);
  and and_3 (S5, A5, B5);
  and and_4 (S4, A4, B4);
  and and_5 (S3, A3, B3);
  and and_6 (S2, A2, B2);
  and and_7 (S1, A1, B1);
  and and_8 (S0, A0, B0);
endmodule

module CompXOR (
  input  A7,
  input  B7,
  input  A6,
  input  B6,
  input  A5,
  input  B5,
  input  A4,
  input  B4,
  input  A3,
  input  B3,
  input  A2,
  input  B2,
  input  A1,
  input  B1,
  input  A0,
  input  B0,
  output S7,
  output S6,
  output S5,
  output S4,
  output S3,
  output S2,
  output S1,
  output S0
);

  xor xor_1 (S7, A7, B7);
  xor xor_2 (S6, A6, B6);
  xor xor_3 (S5, A5, B5);
  xor xor_4 (S4, A4, B4);
  xor xor_5 (S3, A3, B3);
  xor xor_6 (S2, A2, B2);
  xor xor_7 (S1, A1, B1);
  xor xor_8 (S0, A0, B0);
endmodule

module CompNAND (
  input  A7,
  input  B7,
  input  A6,
  input  B6,
  input  A5,
  input  B5,
  input  A4,
  input  B4,
  input  A3,
  input  B3,
  input  A2,
  input  B2,
  input  A1,
  input  B1,
  input  A0,
  input  B0,
  output S7,
  output S6,
  output S5,
  output S4,
  output S3,
  output S2,
  output S1,
  output S0
);

  nand nand_1 (S7, A7, B7);
  nand nand_2 (S6, A6, B6);
  nand nand_3 (S5, A5, B5);
  nand nand_4 (S4, A4, B4);
  nand nand_5 (S3, A3, B3);
  nand nand_6 (S2, A2, B2);
  nand nand_7 (S1, A1, B1);
  nand nand_8 (S0, A0, B0);
endmodule

module SelectorMUX16 (
  input  [3:0] in_1,
  input  [15:0] in_2,
  output S
);

  wire and_1_out, and_2_out, and_3_out, and_4_out, and_5_out, and_6_out, and_7_out, and_8_out, and_9_out,
       and_10_out, and_11_out, and_12_out, and_13_out, and_14_out, and_15_out, and_16_out, not_1_out,
       not_2_out, not_3_out, not_4_out;

  not not_1 (not_1_out, in_1[3]);
  not not_2 (not_2_out, in_1[2]);
  not not_3 (not_3_out, in_1[1]);
  not not_4 (not_4_out, in_1[0]);
  and and_1 (and_1_out, in_2[0], not_4_out, not_3_out, not_2_out, not_1_out);
  and and_2 (and_2_out, in_2[1], in_1[0], not_3_out, not_2_out, not_1_out);
  and and_3 (and_3_out, in_2[2], not_4_out, in_1[1], not_2_out, not_1_out);
  and and_4 (and_4_out, in_2[3], in_1[0], in_1[1], not_2_out, not_1_out);
  and and_5 (and_5_out, in_2[4], not_4_out, not_3_out, in_1[2], not_1_out);
  and and_6 (and_6_out, in_2[5], in_1[0], not_3_out, in_1[2], not_1_out);
  and and_7 (and_7_out, in_2[6], not_4_out, in_1[1], in_1[2], not_1_out);
  and and_8 (and_8_out, in_2[7], in_1[0], in_1[1], in_1[2], not_1_out);
  and and_9 (and_9_out, in_2[8], not_4_out, not_3_out, not_2_out, in_1[3]);
  and and_10 (and_10_out, in_2[9], in_1[0], not_3_out, not_2_out, in_1[3]);
  and and_11 (and_11_out, in_2[10], not_4_out, in_1[1], not_2_out, in_1[3]);
  and and_12 (and_12_out, in_2[11], in_1[0], in_1[1], not_2_out, in_1[3]);
  and and_13 (and_13_out, in_2[12], not_4_out, not_3_out, in_1[2], in_1[3]);
  and and_14 (and_14_out, in_2[13], in_1[0], not_3_out, in_1[2], in_1[3]);
  and and_15 (and_15_out, in_2[14], not_4_out, in_1[1], in_1[2], in_1[3]);
  and and_16 (and_16_out, in_2[15], in_1[0], in_1[1], in_1[2], in_1[3]);
  or or_1 (S, and_1_out, and_2_out, and_3_out, and_4_out, and_5_out, and_6_out, and_7_out, and_8_out, and_9_out, and_10_out, and_11_out, and_12_out, and_13_out, and_14_out, and_15_out, and_16_out);
endmodule

module CompNOR (
  input  A7,
  input  B7,
  input  A6,
  input  B6,
  input  A5,
  input  B5,
  input  A4,
  input  B4,
  input  A3,
  input  B3,
  input  A2,
  input  B2,
  input  A1,
  input  B1,
  input  A0,
  input  B0,
  output S7,
  output S6,
  output S5,
  output S4,
  output S3,
  output S2,
  output S1,
  output S0
);

  nor nor_1 (S7, A7, B7);
  nor nor_2 (S6, A6, B6);
  nor nor_3 (S5, A5, B5);
  nor nor_4 (S4, A4, B4);
  nor nor_5 (S3, A3, B3);
  nor nor_6 (S2, A2, B2);
  nor nor_7 (S1, A1, B1);
  nor nor_8 (S0, A0, B0);
endmodule

module Testeos (
  input  in_1,
  input  [7:0] in_2,
  input  in_3,
  input  in_4,
  output [7:0] out_5,
  output out_6
);

  wire clock_1_out, not_1_out;
  wire [7:0] controlled_buffer_1_out, sumador_1_s0;

  assign controlled_buffer_1_out = in_1 ? in_2 : 8'bz;  // Controlled_Buffer controlled_buffer_1
  not not_1 (not_1_out, in_1);
  assign controlled_buffer_1_out = not_1_out ? sumador_1_s0 : 8'bz;  // Controlled_Buffer controlled_buffer_2
  Register register_1 (.D(controlled_buffer_1_out), .en(clock_1_out), .clk(clock_1_out), .Q(out_5), .clr(in_3));
  Clock clock_1 (.out(clock_1_out));
  Sumador sumador_1 (
    .B1(out_5[1]), .A0(1'b1), .B0(out_5[0]), .A7(1'b0), .B7(out_5[7]), .A6(1'b0), .B6(out_5[6]), .A5(1'b0),
    .B5(out_5[5]), .A4(1'b0), .B4(out_5[4]), .A3(1'b0), .B3(out_5[3]), .A2(1'b0), .B2(out_5[2]), .A1(1'b0),
    .S1(sumador_1_s0[1]), .S0(sumador_1_s0[0]), .S7(sumador_1_s0[7]), .S6(sumador_1_s0[6]),
    .S5(sumador_1_s0[5]), .S4(sumador_1_s0[4]), .S3(sumador_1_s0[3]), .S2(sumador_1_s0[2]));  // open: Cout

  assign out_6 = in_4;

  // Other names for the same wires on the sheet: A = in_4
endmodule

module TESTPANTALLA (
  input  [7:0] in_1,
  input  in_2,
  output [3:0] out_3
);

  wire binary_to_bcd_converter_1_p2, clock_1_out;
  wire [3:0] sumador_1_s0;

  Register #(.width(4)) register_1 (.D(sumador_1_s0), .en(clock_1_out), .clk(clock_1_out), .Q(out_3), .clr(in_2));
  Clock clock_1 (.out(clock_1_out));
  // Binary_to_BCD_converter #(.binvalue(4)) binary_to_bcd_converter_1: pin names not known; wires that end beside it: out_3, binary_to_bcd_converter_1_p2
  Sumador sumador_1 (
    .B1(out_3[1]), .A0(1'b1), .B0(out_3[0]), .A7(1'b0), .B7(1'b0), .A6(1'b0), .B6(1'b0), .A5(1'b0),
    .B5(1'b0), .A4(1'b0), .B4(1'b0), .A3(1'b0), .B3(out_3[3]), .A2(1'b0), .B2(out_3[2]), .A1(1'b0),
    .S1(sumador_1_s0[1]), .S0(sumador_1_s0[0]), .S3(sumador_1_s0[3]), .S2(sumador_1_s0[2]));  // open: Cout, S7, S6, S5, S4
  _7_Segment_Display u_7_segment_display_1 ();  // open: g, f, a, b, e, d, c, dp
  // BCD_to_7_Segment_decoder bcd_to_7_segment_decoder_1: pin names not known; wires that end beside it: binary_to_bcd_converter_1_p2
  _7_Segment_Display u_7_segment_display_2 ();  // open: g, f, a, b, e, d, c, dp
  // BCD_to_7_Segment_decoder bcd_to_7_segment_decoder_2: pin names not known
  // Binary_to_BCD_converter #(.binvalue(8)) binary_to_bcd_converter_2: pin names not known; wires that end beside it: in_1
  _7_Segment_Display u_7_segment_display_3 ();  // open: g, f, a, b, e, d, c, dp
  _7_Segment_Display u_7_segment_display_4 ();  // open: g, f, a, b, e, d, c, dp
  // BCD_to_7_Segment_decoder bcd_to_7_segment_decoder_3: pin names not known
  // BCD_to_7_Segment_decoder bcd_to_7_segment_decoder_4: pin names not known
endmodule
